// Logisim project exp1.circ as structural Verilog: 14 circuits, main circuit main
module main (
  input  [3:0] in_1
);

  DotMatrix #(.inputtype("row"), .matrixcols(16), .matrixrows(16)) dotmatrix_1 (
    .row0(16'h800), .row1(16'hbfc), .row2(16'h840), .row3(16'h1040), .row4(16'h1040), .row5(16'h3040),
    .row6(16'h33f8), .row7(16'h5088), .row8(16'h9088), .row9(16'h1088), .row10(16'h1088), .row11(16'h1108),
    .row12(16'h1108), .row13(16'h1108), .row14(16'h17fe), .row15(16'h1000));
  DotMatrix #(.inputtype("row"), .matrixcols(16), .matrixrows(16)) dotmatrix_2 (
    .row0(16'h100), .row1(16'h100), .row2(16'h100), .row3(16'h920), .row4(16'h910), .row5(16'h1108),
    .row6(16'h1104), .row7(16'h2114), .row8(16'h4110), .row9(16'h120), .row10(16'h40), .row11(16'h80),
    .row12(16'h100), .row13(16'h200), .row14(16'hc00), .row15(16'h7000));
  DotMatrix #(.inputtype("row"), .matrixcols(16), .matrixrows(16)) dotmatrix_3 (
    .row0(16'h2000), .row1(16'h23f8), .row2(16'h2208), .row3(16'h2208), .row4(16'hfb28), .row5(16'h22a8),
    .row6(16'h22a8), .row7(16'h7248), .row8(16'h6a48), .row9(16'ha2a8), .row10(16'ha2a8), .row11(16'h232a),
    .row12(16'h240a), .row13(16'h240a), .row14(16'h2806), .row15(16'h3002));
endmodule

module _2 (
  input  in_1,
  input  in_2,
  input  in_3,
  input  in_4,
  input  in_5,
  input  in_6,
  input  in_7,
  input  in_8,
  input  in_9,
  input  in_10,
  input  in_11,
  input  in_12,
  input  in_13,
  input  in_14,
  input  in_15,
  input  in_16,
  input  in_17,
  input  in_18,
  input  in_19,
  input  in_20,
  input  in_21,
  input  in_22,
  input  in_23,
  input  in_24,
  input  in_25,
  input  in_26,
  input  in_27,
  input  in_28,
  input  in_29,
  input  in_30,
  input  in_31,
  input  in_32,
  input  in_33,
  input  in_34,
  input  in_35,
  input  in_36,
  input  in_37,
  input  in_38,
  input  in_39,
  input  in_40,
  input  in_41,
  input  in_42,
  input  in_43,
  input  in_44,
  input  in_45,
  input  in_46,
  input  in_47,
  input  in_48,
  input  in_49,
  input  in_50,
  input  in_51,
  input  in_52,
  input  in_53,
  input  in_54,
  input  in_55,
  input  in_56,
  input  in_57,
  input  in_58,
  input  in_59,
  input  in_60,
  input  in_61,
  input  in_62,
  input  in_63,
  input  in_64,
  input  in_65,
  input  in_66,
  input  in_67,
  input  in_68,
  input  in_69,
  input  in_70,
  input  in_71,
  input  in_72,
  input  in_73,
  input  in_74,
  input  in_75,
  input  in_76,
  input  in_77,
  input  in_78,
  input  in_79,
  input  in_80
);

  _7_Segment_Display u_7_segment_display_1 (
    .g(in_21), .f(in_1), .a(in_2), .b(in_22), .e(in_41), .d(in_61), .c(in_62), .dp(in_42));
  _7_Segment_Display u_7_segment_display_2 (
    .g(in_23), .f(in_3), .a(in_4), .b(in_24), .e(in_43), .d(in_63), .c(in_64), .dp(in_44));
  _7_Segment_Display u_7_segment_display_3 (
    .g(in_25), .f(in_5), .a(in_6), .b(in_26), .e(in_45), .d(in_65), .c(in_66), .dp(in_46));
  Transistor transistor_1 ();  // open: in, out, gate
  _7_Segment_Display u_7_segment_display_4 (
    .g(in_27), .f(in_7), .a(in_8), .b(in_28), .e(in_47), .d(in_67), .c(in_68), .dp(in_48));
  Transistor #(.\type ("n")) transistor_2 ();  // open: in, out, gate
  _7_Segment_Display u_7_segment_display_5 (
    .g(in_29), .f(in_9), .a(in_10), .b(in_30), .e(in_49), .d(in_69), .c(in_70), .dp(in_50));
  _7_Segment_Display u_7_segment_display_6 (
    .g(in_31), .f(in_11), .a(in_12), .b(in_32), .e(in_51), .d(in_71), .c(in_72), .dp(in_52));
  _7_Segment_Display u_7_segment_display_7 (
    .g(in_33), .f(in_13), .a(in_14), .b(in_34), .e(in_53), .d(in_73), .c(in_74), .dp(in_54));
  _7_Segment_Display u_7_segment_display_8 (
    .g(in_35), .f(in_15), .a(in_16), .b(in_36), .e(in_55), .d(in_75), .c(in_76), .dp(in_56));
  _7_Segment_Display u_7_segment_display_9 (
    .g(in_37), .f(in_17), .a(in_18), .b(in_38), .e(in_57), .d(in_77), .c(in_78), .dp(in_58));
  _7_Segment_Display u_7_segment_display_10 (
    .g(in_39), .f(in_19), .a(in_20), .b(in_40), .e(in_59), .d(in_79), .c(in_80), .dp(in_60));
endmodule

module _3 (
  input  in_1,
  input  in_2,
  input  in_3,
  input  in_4,
  input  in_5,
  input  in_6,
  input  in_7,
  input  in_8,
  input  in_9,
  input  in_10,
  input  in_11,
  input  in_12,
  input  in_13,
  output out_14,
  output out_15,
  output out_16,
  output out_17,
  output out_18,
  output out_19,
  output out_20
);

  wire transistor_1_out, transistor_3_out, transistor_5_out, transistor_8_out, transistor_20_out,
       transistor_21_out, transistor_23_out, transistor_25_out, transistor_26_out, transistor_27_out,
       transistor_28_out, transistor_33_out;

  Transistor #(.\type ("n")) transistor_1 (.in(1'b0), .out(transistor_1_out), .gate(in_2));
  Transistor transistor_2 (.in(transistor_1_out), .out(out_14), .gate(in_1));
  Transistor transistor_3 (.in(1'b0), .out(transistor_3_out), .gate(in_2));
  Transistor #(.\type ("n")) transistor_4 (.in(transistor_3_out), .out(out_14), .gate(in_1));
  Transistor #(.\type ("n")) transistor_5 (.in(1'b1), .out(transistor_5_out), .gate(in_4));
  Transistor transistor_6 (.in(transistor_5_out), .out(out_15), .gate(in_3));
  Transistor #(.\type ("n")) transistor_7 (.in(transistor_8_out), .out(out_15), .gate(in_3));
  Transistor transistor_8 (.in(1'b1), .out(transistor_8_out), .gate(in_4));
  Transistor #(.\type ("n")) transistor_9 (.in(1'b1), .out(out_16), .gate(in_5));
  Transistor #(.\type ("n"), .gate("br")) transistor_10 (.in(1'b1), .out(out_16), .gate(in_6));
  Transistor transistor_11 (.in(1'b0), .out(out_17), .gate(in_7));
  Transistor #(.gate("br")) transistor_12 (.in(1'b0), .out(out_17), .gate(in_8));
  Transistor #(.\type ("n")) transistor_13 (.in(1'b0), .out(out_19), .gate(in_10));
  Transistor #(.\type ("n"), .gate("br")) transistor_14 (.in(1'b0), .out(out_19), .gate(in_11));
  Transistor transistor_15 (.in(transistor_25_out), .out(out_14), .gate(in_1));
  Transistor #(.\type ("n")) transistor_16 (.in(transistor_26_out), .out(out_14), .gate(in_1));
  Transistor transistor_17 (.in(transistor_27_out), .out(out_15), .gate(in_3));
  Transistor #(.\type ("n")) transistor_18 (.in(transistor_28_out), .out(out_15), .gate(in_3));
  Transistor transistor_19 (.in(transistor_20_out), .out(out_16), .gate(in_5));
  Transistor transistor_20 (.in(1'b0), .out(transistor_20_out), .gate(in_6));
  Transistor #(.\type ("n")) transistor_21 (.in(1'b1), .out(transistor_21_out), .gate(in_8));
  Transistor #(.\type ("n")) transistor_22 (.in(transistor_21_out), .out(out_17), .gate(in_7));
  Transistor transistor_23 (.in(1'b1), .out(transistor_23_out), .gate(in_11));
  Transistor transistor_24 (.in(transistor_23_out), .out(out_19), .gate(in_10));
  Transistor transistor_25 (.in(1'b1), .out(transistor_25_out), .gate(in_2));
  Transistor #(.\type ("n")) transistor_26 (.in(1'b1), .out(transistor_26_out), .gate(in_2));
  Transistor transistor_27 (.in(1'b0), .out(transistor_27_out), .gate(in_4));
  Transistor #(.\type ("n")) transistor_28 (.in(1'b0), .out(transistor_28_out), .gate(in_4));
  Transistor #(.\type ("n")) transistor_29 (.in(1'b0), .out(out_18), .gate(in_9));
  Transistor transistor_30 (.in(1'b1), .out(out_20), .gate(in_12));
  Transistor #(.gate("br")) transistor_31 (.in(1'b1), .out(out_20), .gate(in_13));
  Transistor #(.\type ("n")) transistor_32 (.in(transistor_33_out), .out(out_20), .gate(in_12));
  Transistor #(.\type ("n")) transistor_33 (.in(1'b0), .out(transistor_33_out), .gate(in_13));
  Transistor transistor_34 (.in(1'b1), .out(out_18), .gate(in_9));

  // Notes on the sheet:
  //   伍少枫 PE20110007 AND Gate
  //   伍少枫 PE20110007 NAND Gate
  //   伍少枫 PE20110007 XNOR Gate
  //   伍少枫 PE20110007 XOR Gate
  //   伍少枫 PE20110007 OR Gate
  //   伍少枫 PE20110007 NOT Gate
  //   伍少枫 PE20110007 NOR Gate
endmodule

module _4 (
  input  A,
  input  B,
  input  S,
  input  in_4,
  input  in_5,
  input  in_6,
  output L,
  output out_8
);

  wire n3_and_gate_1_out_3, n3_and_gate_2_out_3, n3_and_gate_3_out_3, n3_and_gate_4_out_3, n3_not_1_out_2,
       n3_not_2_out_2;

  _3_NOT_Gate u_3_not_1 (.in_1(S), .out_2(n3_not_1_out_2));
  _3_AND_Gate u_3_and_gate_1 (.in_1(A), .in_2(n3_not_1_out_2), .out_3(n3_and_gate_1_out_3));
  _3_AND_Gate u_3_and_gate_2 (.in_1(B), .in_2(S), .out_3(n3_and_gate_2_out_3));
  _3_NOT_Gate u_3_not_2 (.in_1(in_6), .out_2(n3_not_2_out_2));
  _3_OR_Gate u_3_or_gate_1 (.out_3(L), .in_1(n3_and_gate_1_out_3), .in_2(n3_and_gate_2_out_3));
  _3_AND_Gate u_3_and_gate_3 (.in_1(in_4), .in_2(n3_not_2_out_2), .out_3(n3_and_gate_3_out_3));
  _3_AND_Gate u_3_and_gate_4 (.in_1(in_5), .in_2(in_6), .out_3(n3_and_gate_4_out_3));
  _3_OR_Gate u_3_or_gate_2 (.out_3(out_8), .in_1(n3_and_gate_3_out_3), .in_2(n3_and_gate_4_out_3));

  // Notes on the sheet:
  //   1 bit 二选一选择器
endmodule

module _3_NOT_Gate (
  input  in_1,
  output out_2
);

  Transistor #(.\type ("n")) transistor_1 (.in(1'b0), .out(out_2), .gate(in_1));
  Transistor transistor_2 (.in(1'b1), .out(out_2), .gate(in_1));

  // Notes on the sheet:
  //   伍少枫 PE20110007 NOT Gate
endmodule

module _3_AND_Gate (
  input  in_1,
  input  in_2,
  output out_3
);

  wire transistor_4_out;

  Transistor transistor_1 (.in(1'b0), .out(out_3), .gate(in_1));
  Transistor #(.gate("br")) transistor_2 (.in(1'b0), .out(out_3), .gate(in_2));
  Transistor #(.\type ("n")) transistor_3 (.in(transistor_4_out), .out(out_3), .gate(in_1));
  Transistor #(.\type ("n")) transistor_4 (.in(1'b1), .out(transistor_4_out), .gate(in_2));

  // Notes on the sheet:
  //   伍少枫 PE20110007 AND Gate
endmodule

module _3_OR_Gate (
  input  in_1,
  input  in_2,
  output out_3
);

  wire transistor_4_out;

  Transistor #(.\type ("n")) transistor_1 (.in(1'b1), .out(out_3), .gate(in_1));
  Transistor #(.\type ("n"), .gate("br")) transistor_2 (.in(1'b1), .out(out_3), .gate(in_2));
  Transistor transistor_3 (.in(transistor_4_out), .out(out_3), .gate(in_1));
  Transistor transistor_4 (.in(1'b0), .out(transistor_4_out), .gate(in_2));

  // Notes on the sheet:
  //   伍少枫 PE20110007 OR Gate
endmodule

module _4_2 (
  input  S1,
  input  S2,
  input  D1,
  input  D4,
  input  D3,
  input  D2,
  input  D1_prime,
  input  D4_prime,
  input  D3_prime,
  input  D2_prime,
  input  in_11,
  input  in_12,
  input  in_13,
  input  in_14,
  input  in_15,
  input  in_16,
  output out_17,
  output out_18,
  output out_19
);

  wire n3_and_gate_1_out_3, n3_and_gate_2_out_3, n3_and_gate_3_out_3, n3_and_gate_4_out_3,
       n3_and_gate_5_out_3, n3_and_gate_6_out_3, n3_and_gate_7_out_3, n3_and_gate_8_out_3,
       n3_and_gate_9_out_3, n3_and_gate_10_out_3, n3_and_gate_11_out_3, n3_and_gate_12_out_3,
       n3_and_gate_13_out_3, n3_and_gate_14_out_3, n3_and_gate_15_out_3, n3_and_gate_16_out_3,
       n3_and_gate_17_out_3, n3_and_gate_18_out_3, n3_and_gate_19_out_3, n3_and_gate_20_out_3,
       n3_and_gate_21_out_3, n3_and_gate_22_out_3, n3_and_gate_23_out_3, n3_and_gate_24_out_3,
       n3_not_1_out_2, n3_not_2_out_2, n3_not_3_out_2, n3_not_4_out_2, n3_not_5_out_2, n3_not_6_out_2,
       n3_or_gate_1_out_3, n3_or_gate_2_out_3, n3_or_gate_3_out_3, n3_or_gate_4_out_3, n3_or_gate_7_out_3,
       n3_or_gate_9_out_3;

  _3_NOT_Gate u_3_not_1 (.in_1(in_11), .out_2(n3_not_1_out_2));
  _3_NOT_Gate u_3_not_2 (.in_1(in_12), .out_2(n3_not_2_out_2));
  _3_NOT_Gate u_3_not_3 (.in_1(S1), .out_2(n3_not_3_out_2));
  _3_NOT_Gate u_3_not_4 (.in_1(S2), .out_2(n3_not_4_out_2));
  _3_AND_Gate u_3_and_gate_1 (.in_1(n3_not_5_out_2), .in_2(n3_not_6_out_2), .out_3(n3_and_gate_1_out_3));
  _3_NOT_Gate u_3_not_5 (.in_1(S1), .out_2(n3_not_5_out_2));
  _3_AND_Gate u_3_and_gate_2 (.in_1(S1), .in_2(n3_not_6_out_2), .out_3(n3_and_gate_2_out_3));
  _3_AND_Gate u_3_and_gate_3 (.in_1(n3_not_5_out_2), .in_2(S2), .out_3(n3_and_gate_3_out_3));
  _3_NOT_Gate u_3_not_6 (.in_1(S2), .out_2(n3_not_6_out_2));
  _3_AND_Gate u_3_and_gate_4 (.in_1(S1), .in_2(S2), .out_3(n3_and_gate_4_out_3));
  _3_AND_Gate u_3_and_gate_5 (.in_1(in_11), .in_2(in_12), .out_3(n3_and_gate_5_out_3));
  _3_AND_Gate u_3_and_gate_6 (.in_1(n3_not_3_out_2), .in_2(n3_not_4_out_2), .out_3(n3_and_gate_6_out_3));
  _3_AND_Gate u_3_and_gate_7 (.in_1(n3_and_gate_6_out_3), .in_2(D1), .out_3(n3_and_gate_7_out_3));
  _3_AND_Gate u_3_and_gate_8 (.in_1(S1), .in_2(n3_not_4_out_2), .out_3(n3_and_gate_8_out_3));
  _3_AND_Gate u_3_and_gate_9 (.in_1(n3_not_3_out_2), .in_2(S2), .out_3(n3_and_gate_9_out_3));
  _3_AND_Gate u_3_and_gate_10 (.in_1(S1), .in_2(S2), .out_3(n3_and_gate_10_out_3));
  _3_AND_Gate u_3_and_gate_11 (.in_1(n3_and_gate_1_out_3), .in_2(D1_prime), .out_3(n3_and_gate_11_out_3));
  _3_AND_Gate u_3_and_gate_12 (.in_1(n3_not_1_out_2), .in_2(n3_not_2_out_2), .out_3(n3_and_gate_12_out_3));
  _3_AND_Gate u_3_and_gate_13 (.in_1(n3_and_gate_5_out_3), .in_2(in_13), .out_3(n3_and_gate_13_out_3));
  _3_AND_Gate u_3_and_gate_14 (.in_1(n3_and_gate_8_out_3), .in_2(D4), .out_3(n3_and_gate_14_out_3));
  _3_AND_Gate u_3_and_gate_15 (.in_1(n3_and_gate_9_out_3), .in_2(D3), .out_3(n3_and_gate_15_out_3));
  _3_AND_Gate u_3_and_gate_16 (.in_1(n3_and_gate_10_out_3), .in_2(D2), .out_3(n3_and_gate_16_out_3));
  _3_AND_Gate u_3_and_gate_17 (.in_1(n3_and_gate_2_out_3), .in_2(D4_prime), .out_3(n3_and_gate_17_out_3));
  _3_AND_Gate u_3_and_gate_18 (.in_1(n3_and_gate_3_out_3), .in_2(D3_prime), .out_3(n3_and_gate_18_out_3));
  _3_AND_Gate u_3_and_gate_19 (.in_1(n3_and_gate_4_out_3), .in_2(D2_prime), .out_3(n3_and_gate_19_out_3));
  _3_AND_Gate u_3_and_gate_20 (.in_1(n3_and_gate_12_out_3), .in_2(in_14), .out_3(n3_and_gate_20_out_3));
  _3_AND_Gate u_3_and_gate_21 (.in_1(in_12), .in_2(n3_not_1_out_2), .out_3(n3_and_gate_21_out_3));
  _3_AND_Gate u_3_and_gate_22 (.in_1(n3_and_gate_21_out_3), .in_2(in_15), .out_3(n3_and_gate_22_out_3));
  _3_OR_Gate u_3_or_gate_1 (.out_3(n3_or_gate_1_out_3), .in_1(n3_and_gate_7_out_3), .in_2(n3_and_gate_14_out_3));
  _3_OR_Gate u_3_or_gate_2 (.out_3(n3_or_gate_2_out_3), .in_1(n3_and_gate_15_out_3), .in_2(n3_and_gate_16_out_3));
  _3_OR_Gate u_3_or_gate_3 (.out_3(n3_or_gate_3_out_3), .in_1(n3_and_gate_11_out_3), .in_2(n3_and_gate_17_out_3));
  _3_OR_Gate u_3_or_gate_4 (.out_3(n3_or_gate_4_out_3), .in_1(n3_and_gate_18_out_3), .in_2(n3_and_gate_19_out_3));
  _3_AND_Gate u_3_and_gate_23 (.in_1(in_11), .in_2(n3_not_2_out_2), .out_3(n3_and_gate_23_out_3));
  _3_OR_Gate u_3_or_gate_5 (.out_3(out_17), .in_1(n3_or_gate_1_out_3), .in_2(n3_or_gate_2_out_3));
  _3_OR_Gate u_3_or_gate_6 (.out_3(out_18), .in_1(n3_or_gate_3_out_3), .in_2(n3_or_gate_4_out_3));
  _3_AND_Gate u_3_and_gate_24 (.in_1(n3_and_gate_23_out_3), .in_2(in_16), .out_3(n3_and_gate_24_out_3));
  _3_OR_Gate u_3_or_gate_7 (.out_3(n3_or_gate_7_out_3), .in_1(n3_and_gate_24_out_3), .in_2(n3_and_gate_20_out_3));
  _3_OR_Gate u_3_or_gate_8 (.out_3(out_19), .in_1(n3_or_gate_7_out_3), .in_2(n3_or_gate_9_out_3));
  _3_OR_Gate u_3_or_gate_9 (.out_3(n3_or_gate_9_out_3), .in_1(n3_and_gate_22_out_3), .in_2(n3_and_gate_13_out_3));

  // Notes on the sheet:
  //   S1
  //   S2
  //   2bit四选一选择器
  //   PE20110007 伍少枫
endmodule

module _4_3 (
  input  in_1,
  input  in_2,
  input  in_3,
  input  in_4,
  input  in_5,
  input  in_6,
  output out_7
);

  wire n3_and_gate_1_out_3, n3_and_gate_2_out_3, n3_not_1_out_2, n3_not_2_out_2, n3_or_gate_1_out_3, n4_1_l,
       n4_2_l;

  _4 u_4_1 (.A(in_1), .L(n4_1_l), .B(in_2), .S(in_3));  // open: in_4, in_5, in_6, out_8
  _4 u_4_2 (.A(in_4), .L(n4_2_l), .B(in_5), .S(in_6));  // open: in_4, in_5, in_6, out_8
  _3_NOT_Gate u_3_not_1 (.in_1(in_3), .out_2(n3_not_1_out_2));
  _3_NOT_Gate u_3_not_2 (.in_1(in_6), .out_2(n3_not_2_out_2));
  _3_AND_Gate u_3_and_gate_1 (.in_1(n3_not_1_out_2), .in_2(in_6), .out_3(n3_and_gate_1_out_3));
  _3_AND_Gate u_3_and_gate_2 (.in_1(in_3), .in_2(n3_not_2_out_2), .out_3(n3_and_gate_2_out_3));
  _3_OR_Gate u_3_or_gate_1 (.out_3(n3_or_gate_1_out_3), .in_1(n3_and_gate_1_out_3), .in_2(n3_and_gate_2_out_3));
  _4 u_4_3 (.A(n4_1_l), .L(out_7), .B(n4_2_l), .S(n3_or_gate_1_out_3));  // open: in_4, in_5, in_6, out_8

  // Notes on the sheet:
  //   用1bit二选一选择器组合成的2bit四选一选择器
  //   PE20110007 伍少枫
endmodule

module _3_NAND_Gate (
  input  in_1,
  input  in_2,
  output out_3
);

  wire transistor_4_out;

  Transistor #(.\type ("n")) transistor_1 (.in(1'b0), .out(out_3), .gate(in_1));
  Transistor #(.\type ("n"), .gate("br")) transistor_2 (.in(1'b0), .out(out_3), .gate(in_2));
  Transistor transistor_3 (.in(transistor_4_out), .out(out_3), .gate(in_1));
  Transistor transistor_4 (.in(1'b1), .out(transistor_4_out), .gate(in_2));

  // Notes on the sheet:
  //   伍少枫 PE20110007 NAND Gate
endmodule

module _3_NOR_Gate (
  input  in_1,
  input  in_2,
  output out_3
);

  wire transistor_4_out;

  Transistor transistor_1 (.in(1'b1), .out(out_3), .gate(in_1));
  Transistor #(.gate("br")) transistor_2 (.in(1'b1), .out(out_3), .gate(in_2));
  Transistor #(.\type ("n")) transistor_3 (.in(transistor_4_out), .out(out_3), .gate(in_1));
  Transistor #(.\type ("n")) transistor_4 (.in(1'b0), .out(transistor_4_out), .gate(in_2));

  // Notes on the sheet:
  //   伍少枫 PE20110007 NOR Gate
endmodule

module _3_XNOR_Gate (
  input  in_1,
  input  in_2,
  input  in_3,
  input  in_4,
  output out_5,
  output out_6
);

  wire and_1_out, and_2_out, not_1_out, not_2_out, transistor_1_out, transistor_2_out, transistor_7_out,
       transistor_8_out;

  Transistor #(.\type ("n")) transistor_1 (.in(1'b0), .out(transistor_1_out), .gate(in_2));
  Transistor transistor_2 (.in(1'b0), .out(transistor_2_out), .gate(in_2));
  Transistor transistor_3 (.in(transistor_1_out), .out(out_5), .gate(in_1));
  Transistor #(.\type ("n")) transistor_4 (.in(transistor_2_out), .out(out_5), .gate(in_1));
  Transistor transistor_5 (.in(transistor_7_out), .out(out_5), .gate(in_1));
  Transistor #(.\type ("n")) transistor_6 (.in(transistor_8_out), .out(out_5), .gate(in_1));
  not not_1 (not_1_out, in_3);
  not not_2 (not_2_out, in_4);
  Transistor transistor_7 (.in(1'b1), .out(transistor_7_out), .gate(in_2));
  Transistor #(.\type ("n")) transistor_8 (.in(1'b1), .out(transistor_8_out), .gate(in_2));
  and and_1 (and_1_out, not_1_out, not_2_out);
  and and_2 (and_2_out, in_3, in_4);
  or or_1 (out_6, and_1_out, and_2_out);

  // Notes on the sheet:
  //   伍少枫 PE20110007 XNOR Gate
endmodule

module _3_XOR_GATE (
  input  in_1,
  input  in_2,
  input  in_3,
  input  in_4,
  output out_5,
  output out_6
);

  wire and_1_out, and_2_out, not_1_out, not_2_out, transistor_1_out, transistor_2_out, transistor_7_out,
       transistor_8_out;

  Transistor #(.\type ("n")) transistor_1 (.in(1'b1), .out(transistor_1_out), .gate(in_2));
  Transistor transistor_2 (.in(1'b1), .out(transistor_2_out), .gate(in_2));
  Transistor transistor_3 (.in(transistor_1_out), .out(out_5), .gate(in_1));
  Transistor #(.\type ("n")) transistor_4 (.in(transistor_2_out), .out(out_5), .gate(in_1));
  not not_1 (not_1_out, in_3);
  and and_1 (and_1_out, not_1_out, in_4);
  not not_2 (not_2_out, in_4);
  Transistor transistor_5 (.in(transistor_7_out), .out(out_5), .gate(in_1));
  Transistor #(.\type ("n")) transistor_6 (.in(transistor_8_out), .out(out_5), .gate(in_1));
  and and_2 (and_2_out, in_3, not_2_out);
  Transistor transistor_7 (.in(1'b0), .out(transistor_7_out), .gate(in_2));
  Transistor #(.\type ("n")) transistor_8 (.in(1'b0), .out(transistor_8_out), .gate(in_2));
  or or_1 (out_6, and_2_out, and_1_out);

  // Notes on the sheet:
  //   伍少枫 PE20110007 XOR Gate
endmodule

module Test (
  input  \输入管脚 ,
  input  [3:0] \多位宽输入 ,
  input  [7:0] in_3,
  input  [1:0] \与门 ,
  input  [1:0] in_5,
  input  in_6,
  input  in_7,
  input  A,
  input  B,
  output \输出管脚 ,
  output [3:0] \多位宽输出 ,
  output [1:0] out_12,
  output [3:0] out_13,
  output [3:0] out_14,
  output [1:0] out_15,
  output [1:0] out_16,
  output [3:0] out_17,
  output [3:0] out_18,
  output [5:0] out_19,
  output [1:0] out_20,
  output [1:0] out_21,
  output [2:0] out_22,
  output [2:0] out_23,
  output Sum,
  output Count
);

  wire button_1_out;

  Button button_1 (.out(button_1_out));
  // Probe on \多位宽输入 
  assign out_22[1:0] = \与门  & in_5;  // AND_Gate and_1, 2 bits wide
  or or_1 (out_22[2], in_6, in_7);
  // Probe on \多位宽输入 
  // Probe on \多位宽输入 
  LED led_1 (.in(button_1_out));
  // Probe on \多位宽输入 
  // Probe on \多位宽输入 
  assign out_23 = ~out_22;  // NOT_Gate not_1, 3 bits wide
  xor xor_1 (Sum, A, B);
  and and_2 (Count, A, B);

  assign out_12 = in_3[1:0];
  assign out_13 = in_3[3:0];
  assign out_14 = in_3[7:4];
  assign out_15 = in_3[1:0];
  assign out_16 = in_3[3:2];
  assign out_17 = in_3[7:4];
  assign out_18 = in_3[3:0];
  assign out_19 = in_3[7:2];
  assign out_20 = in_3[5:4];
  assign out_21 = in_3[7:6];
  assign \多位宽输出  = \多位宽输入 ;
  assign \输出管脚  = \输入管脚 ;

  // Notes on the sheet:
  //   按钮
  //   或门
  //   分线器
  //   LED
  //   非门
  //   探针(不同进制)
  //   伍少枫 PE20110007
endmodule
