// Logisim project exp2.circ as structural Verilog
module \生成电路  (
  input  I4,
  input  I3,
  input  I2,
  input  I1,
  output O4,
  output O3,
  output O2,
  output O1
);

  wire and_1_out, and_2_out, and_3_out, and_4_out, and_5_out, and_6_out, and_7_out, and_8_out, and_9_out,
       and_10_out, and_11_out, and_12_out, and_13_out, and_14_out, not_1_out, not_2_out, not_3_out,
       not_4_out, not_5_out, not_6_out, not_7_out, not_8_out, not_9_out, not_10_out, not_11_out, not_12_out,
       not_13_out, not_14_out, not_15_out, not_16_out, not_17_out, not_18_out, not_19_out, not_20_out,
       not_21_out, not_22_out, not_23_out, not_24_out;

  not not_1 (not_1_out, I4);
  and and_1 (and_1_out, not_1_out, I3);
  and and_2 (and_2_out, I4, not_2_out);
  not not_2 (not_2_out, I3);
  not not_3 (not_3_out, I4);
  and and_3 (and_3_out, not_3_out, not_4_out, I2);
  not not_4 (not_4_out, I3);
  not not_5 (not_5_out, I4);
  and and_4 (and_4_out, not_5_out, I3, not_6_out);
  not not_6 (not_6_out, I2);
  and and_5 (and_5_out, I4, not_7_out, not_8_out);
  not not_7 (not_7_out, I3);
  not not_8 (not_8_out, I2);
  and and_6 (and_6_out, I4, I3, I2);
  not not_9 (not_9_out, I4);
  not not_10 (not_10_out, I3);
  not not_11 (not_11_out, I2);
  not not_12 (not_12_out, I4);
  not not_13 (not_13_out, I3);
  not not_14 (not_14_out, I1);
  not not_15 (not_15_out, I4);
  not not_16 (not_16_out, I2);
  not not_17 (not_17_out, I1);
  not not_18 (not_18_out, I4);
  not not_19 (not_19_out, I3);
  not not_20 (not_20_out, I2);
  not not_21 (not_21_out, I1);
  not not_22 (not_22_out, I3);
  not not_23 (not_23_out, I2);
  not not_24 (not_24_out, I1);
  or or_1 (O3, and_1_out, and_2_out);
  or or_2 (O2, and_3_out, and_4_out, and_5_out, and_6_out);
  and and_7 (and_7_out, not_9_out, not_10_out, not_11_out, I1);
  and and_8 (and_8_out, not_12_out, not_13_out, I2, not_14_out);
  and and_9 (and_9_out, not_15_out, I3, not_16_out, not_17_out);
  and and_10 (and_10_out, not_18_out, I3, I2, I1);
  and and_11 (and_11_out, I4, not_19_out, not_20_out, not_21_out);
  and and_12 (and_12_out, I4, not_22_out, I2, I1);
  and and_13 (and_13_out, I4, I3, not_23_out, I1);
  and and_14 (and_14_out, I4, I3, I2, not_24_out);
  or or_3 (O1, and_7_out, and_8_out, and_9_out, and_10_out, and_11_out, and_12_out, and_13_out, and_14_out);

  assign O4 = I4;
endmodule

module \生成电路2  (
  input  A,
  input  B,
  input  C,
  input  D,
  input  S1,
  input  S2,
  output L
);

  wire and_1_out, and_2_out, and_3_out, and_4_out, not_1_out, not_2_out, not_3_out, not_4_out;

  not not_1 (not_1_out, S1);
  not not_2 (not_2_out, S2);
  not not_3 (not_3_out, S1);
  not not_4 (not_4_out, S2);
  and and_1 (and_1_out, not_1_out, not_2_out, A);
  and and_2 (and_2_out, not_3_out, S2, C);
  and and_3 (and_3_out, S1, not_4_out, D);
  and and_4 (and_4_out, S1, S2, B);
  or or_1 (L, and_1_out, and_2_out, and_3_out, and_4_out);
endmodule

module \生成电路3  (
  input  i7,
  input  i6,
  input  i5,
  input  i4,
  input  i3,
  input  i2,
  input  i1,
  output y2,
  output y1,
  output y0
);
endmodule

module \生成电路3_1  (
  input  i7,
  input  i6,
  input  i5,
  input  i4,
  input  i3,
  input  i2,
  input  i1,
  output y2,
  output y1,
  output y0
);

  wire and_1_out, and_2_out, and_3_out, and_4_out, and_5_out, and_6_out, and_7_out, and_8_out, and_9_out,
       not_1_out, not_2_out, not_3_out, not_4_out, not_5_out, not_6_out, not_7_out, not_8_out, not_9_out,
       not_10_out, not_11_out, not_12_out, not_13_out, not_14_out, not_15_out, not_16_out, not_17_out,
       not_18_out, not_19_out, not_20_out, not_21_out, not_22_out, not_23_out, not_24_out, not_25_out,
       not_26_out, not_27_out, not_28_out;

  not not_1 (not_1_out, i7);
  not not_2 (not_2_out, i7);
  not not_3 (not_3_out, i6);
  not not_4 (not_4_out, i7);
  not not_5 (not_5_out, i6);
  not not_6 (not_6_out, i5);
  not not_7 (not_7_out, i7);
  not not_8 (not_8_out, i6);
  not not_9 (not_9_out, i5);
  not not_10 (not_10_out, i4);
  not not_11 (not_11_out, i7);
  not not_12 (not_12_out, i6);
  not not_13 (not_13_out, i5);
  not not_14 (not_14_out, i4);
  not not_15 (not_15_out, i3);
  not not_16 (not_16_out, i7);
  not not_17 (not_17_out, i6);
  not not_18 (not_18_out, i5);
  not not_19 (not_19_out, i4);
  not not_20 (not_20_out, i7);
  not not_21 (not_21_out, i6);
  not not_22 (not_22_out, i5);
  not not_23 (not_23_out, i4);
  not not_24 (not_24_out, i3);
  not not_25 (not_25_out, i2);
  and and_1 (and_1_out, not_1_out, i6);
  and and_2 (and_2_out, not_2_out, not_3_out, i5);
  and and_3 (and_3_out, not_4_out, not_5_out, not_6_out, i4);
  not not_26 (not_26_out, i7);
  and and_4 (and_4_out, not_26_out, i6);
  and and_5 (and_5_out, not_7_out, not_8_out, not_9_out, not_10_out, i3);
  and and_6 (and_6_out, not_11_out, not_12_out, not_13_out, not_14_out, not_15_out, i2);
  not not_27 (not_27_out, i7);
  not not_28 (not_28_out, i6);
  and and_7 (and_7_out, not_27_out, not_28_out, i5);
  and and_8 (and_8_out, not_16_out, not_17_out, not_18_out, not_19_out, i3);
  and and_9 (and_9_out, not_20_out, not_21_out, not_22_out, not_23_out, not_24_out, not_25_out, i1);
  or or_1 (y2, i7, and_1_out, and_2_out, and_3_out);
  or or_2 (y1, i7, and_4_out, and_5_out, and_6_out);
  or or_3 (y0, i7, and_7_out, and_8_out, and_9_out);
endmodule

module \生成电路3_2  (
  input  i7,
  input  i6,
  input  i5,
  input  i4,
  input  i3,
  input  i2,
  input  i1,
  output y2,
  output y1,
  output y0
);

  wire and_1_out, and_2_out, and_3_out, and_4_out, and_5_out, not_1_out, not_2_out, not_3_out, not_4_out,
       not_5_out, not_6_out, not_7_out, not_8_out, not_9_out, not_10_out;

  or or_1 (y2, i4, i5, i6, i7);
  not not_1 (not_1_out, i5);
  not not_2 (not_2_out, i4);
  not not_3 (not_3_out, i5);
  not not_4 (not_4_out, i4);
  not not_5 (not_5_out, i6);
  not not_6 (not_6_out, i4);
  not not_7 (not_7_out, i2);
  not not_8 (not_8_out, i6);
  not not_9 (not_9_out, i4);
  not not_10 (not_10_out, i6);
  and and_1 (and_1_out, not_1_out, not_2_out, i2);
  and and_2 (and_2_out, not_3_out, not_4_out, i3);
  and and_3 (and_3_out, not_5_out, not_6_out, not_7_out, i1);
  and and_4 (and_4_out, not_8_out, not_9_out, i3);
  and and_5 (and_5_out, not_10_out, i5);
  or or_2 (y1, and_1_out, and_2_out, i6, i7);
  or or_3 (y0, and_3_out, and_4_out, and_5_out, i7);
endmodule

module exercise1 (
  input  Ci_1,
  input  Ai,
  input  Bi,
  output Si,
  output Ci
);


  // Notes on the sheet:
  //   伍少枫 PE20110007
endmodule

module exercise1_1 (
  input  Ci1,
  input  Ai,
  input  Bi,
  output Si,
  output Ci
);

  wire and_1_out, and_2_out, and_3_out, and_4_out, and_5_out, and_6_out, and_7_out, not_1_out, not_2_out,
       not_3_out, not_4_out, not_5_out, not_6_out;

  not not_1 (not_1_out, Ci1);
  not not_2 (not_2_out, Ai);
  not not_3 (not_3_out, Ci1);
  not not_4 (not_4_out, Bi);
  not not_5 (not_5_out, Ai);
  not not_6 (not_6_out, Bi);
  and and_1 (and_1_out, Ai, Bi);
  and and_2 (and_2_out, Ci1, Bi);
  and and_3 (and_3_out, Ci1, Ai);
  and and_4 (and_4_out, not_1_out, not_2_out, Bi);
  and and_5 (and_5_out, not_3_out, Ai, not_4_out);
  and and_6 (and_6_out, Ci1, not_5_out, not_6_out);
  and and_7 (and_7_out, Ci1, Ai, Bi);
  or or_1 (Ci, and_1_out, and_2_out, and_3_out);
  or or_2 (Si, and_4_out, and_5_out, and_6_out, and_7_out);

  // Notes on the sheet:
  //   伍少枫 PE20110007
endmodule

module exercise2 (
  input  G1,
  input  G2,
  input  G3,
  input  A2,
  input  A1,
  input  A0,
  output Y7,
  output Y6,
  output Y5,
  output Y4,
  output Y3,
  output Y2,
  output Y1,
  output Y0
);
endmodule

module exercise2_1 (
  input  G1,
  input  G2,
  input  G3,
  input  A2,
  input  A1,
  input  A0,
  output Y7,
  output Y6,
  output Y5,
  output Y4,
  output Y3,
  output Y2,
  output Y1,
  output Y0
);

  wire and_1_out, and_2_out, and_3_out, and_4_out, and_5_out, and_6_out, and_7_out, and_8_out, and_9_out,
       and_10_out, and_11_out, and_12_out, and_13_out, and_14_out, and_15_out, and_16_out, and_17_out,
       and_18_out, and_19_out, and_20_out, and_21_out, and_22_out, and_23_out, and_24_out, and_25_out,
       and_26_out, and_27_out, and_28_out, and_29_out, and_30_out, and_31_out, and_32_out, and_33_out,
       and_34_out, and_35_out, and_36_out, and_37_out, and_38_out, and_39_out, and_40_out, and_41_out,
       and_42_out, and_43_out, and_44_out, and_45_out, and_46_out, and_47_out, and_48_out, and_49_out,
       and_50_out, and_51_out, and_52_out, and_53_out, and_54_out, and_55_out, and_56_out, not_1_out,
       not_2_out, not_3_out, not_4_out, not_5_out, not_6_out, not_7_out, not_8_out, not_9_out, not_10_out,
       not_11_out, not_12_out, not_13_out, not_14_out, not_15_out, not_16_out, not_17_out, not_18_out,
       not_19_out, not_20_out, not_21_out, not_22_out, not_23_out, not_24_out, not_25_out, not_26_out,
       not_27_out, not_28_out, not_29_out, not_30_out, not_31_out, not_32_out, not_33_out, not_34_out,
       not_35_out, not_36_out, not_37_out, not_38_out, not_39_out, not_40_out, not_41_out, not_42_out,
       not_43_out, not_44_out, not_45_out, not_46_out, not_47_out, not_48_out, not_49_out, not_50_out,
       not_51_out, not_52_out, not_53_out, not_54_out, not_55_out, not_56_out, not_57_out, not_58_out,
       not_59_out, not_60_out, not_61_out, not_62_out, not_63_out, not_64_out, not_65_out, not_66_out,
       not_67_out, not_68_out, not_69_out, not_70_out, not_71_out, not_72_out, not_73_out, not_74_out,
       not_75_out, not_76_out, not_77_out, not_78_out, not_79_out, not_80_out, not_81_out, not_82_out,
       not_83_out, not_84_out, not_85_out, not_86_out, not_87_out, not_88_out, not_89_out, not_90_out,
       not_91_out, not_92_out, not_93_out, not_94_out, not_95_out, not_96_out, not_97_out, not_98_out,
       not_99_out, not_100_out, not_101_out, not_102_out, not_103_out, not_104_out, not_105_out, not_106_out,
       not_107_out, not_108_out, not_109_out, not_110_out, not_111_out, not_112_out, not_113_out,
       not_114_out, not_115_out, not_116_out, not_117_out, not_118_out, not_119_out, not_120_out,
       not_121_out, not_122_out, not_123_out, not_124_out, not_125_out, not_126_out, not_127_out,
       not_128_out, not_129_out, not_130_out, not_131_out, not_132_out, not_133_out, not_134_out,
       not_135_out, not_136_out, not_137_out, not_138_out, not_139_out, not_140_out, not_141_out,
       not_142_out, not_143_out, not_144_out, not_145_out, not_146_out, not_147_out, not_148_out,
       not_149_out, not_150_out, not_151_out, not_152_out, not_153_out, not_154_out, not_155_out,
       not_156_out, not_157_out, not_158_out, not_159_out, not_160_out, not_161_out, not_162_out,
       not_163_out, not_164_out, not_165_out, not_166_out, not_167_out, not_168_out, not_169_out,
       not_170_out, not_171_out, not_172_out, not_173_out, not_174_out, not_175_out, not_176_out,
       not_177_out, not_178_out, not_179_out, not_180_out, not_181_out, not_182_out, not_183_out,
       not_184_out, not_185_out, not_186_out, not_187_out, not_188_out, not_189_out, not_190_out,
       not_191_out, not_192_out, not_193_out, not_194_out, not_195_out, not_196_out, not_197_out,
       not_198_out, not_199_out, not_200_out, not_201_out, not_202_out, not_203_out, not_204_out;

  not not_1 (not_1_out, G2);
  not not_2 (not_2_out, G3);
  not not_3 (not_3_out, A2);
  not not_4 (not_4_out, A1);
  not not_5 (not_5_out, A0);
  not not_6 (not_6_out, G2);
  not not_7 (not_7_out, G3);
  not not_8 (not_8_out, A2);
  not not_9 (not_9_out, A1);
  not not_10 (not_10_out, G2);
  not not_11 (not_11_out, G3);
  not not_12 (not_12_out, A2);
  not not_13 (not_13_out, A0);
  not not_14 (not_14_out, G2);
  not not_15 (not_15_out, G3);
  not not_16 (not_16_out, A2);
  not not_17 (not_17_out, G2);
  not not_18 (not_18_out, G3);
  not not_19 (not_19_out, A1);
  not not_20 (not_20_out, A0);
  not not_21 (not_21_out, G2);
  not not_22 (not_22_out, G3);
  not not_23 (not_23_out, A1);
  not not_24 (not_24_out, G2);
  not not_25 (not_25_out, G3);
  not not_26 (not_26_out, A0);
  not not_27 (not_27_out, G2);
  not not_28 (not_28_out, G3);
  not not_29 (not_29_out, A2);
  not not_30 (not_30_out, A1);
  not not_31 (not_31_out, A0);
  not not_32 (not_32_out, G2);
  not not_33 (not_33_out, G3);
  not not_34 (not_34_out, A2);
  not not_35 (not_35_out, A1);
  not not_36 (not_36_out, G2);
  not not_37 (not_37_out, G3);
  not not_38 (not_38_out, A2);
  not not_39 (not_39_out, A0);
  not not_40 (not_40_out, G2);
  not not_41 (not_41_out, G3);
  not not_42 (not_42_out, A2);
  not not_43 (not_43_out, G2);
  not not_44 (not_44_out, G3);
  not not_45 (not_45_out, A1);
  not not_46 (not_46_out, A0);
  not not_47 (not_47_out, G2);
  not not_48 (not_48_out, G3);
  not not_49 (not_49_out, A1);
  not not_50 (not_50_out, G2);
  not not_51 (not_51_out, G3);
  not not_52 (not_52_out, G2);
  not not_53 (not_53_out, G3);
  not not_54 (not_54_out, A2);
  not not_55 (not_55_out, A1);
  not not_56 (not_56_out, A0);
  not not_57 (not_57_out, G2);
  not not_58 (not_58_out, G3);
  not not_59 (not_59_out, A2);
  not not_60 (not_60_out, A1);
  not not_61 (not_61_out, G2);
  not not_62 (not_62_out, G3);
  not not_63 (not_63_out, A2);
  not not_64 (not_64_out, A0);
  not not_65 (not_65_out, G2);
  not not_66 (not_66_out, G3);
  not not_67 (not_67_out, A2);
  not not_68 (not_68_out, G2);
  not not_69 (not_69_out, G3);
  not not_70 (not_70_out, A1);
  not not_71 (not_71_out, A0);
  not not_72 (not_72_out, G2);
  not not_73 (not_73_out, G3);
  not not_74 (not_74_out, A0);
  not not_75 (not_75_out, G2);
  not not_76 (not_76_out, G3);
  not not_77 (not_77_out, G2);
  not not_78 (not_78_out, G3);
  not not_79 (not_79_out, A2);
  not not_80 (not_80_out, A1);
  not not_81 (not_81_out, A0);
  not not_82 (not_82_out, G2);
  not not_83 (not_83_out, G3);
  not not_84 (not_84_out, A2);
  not not_85 (not_85_out, A1);
  not not_86 (not_86_out, G2);
  not not_87 (not_87_out, G3);
  not not_88 (not_88_out, A2);
  not not_89 (not_89_out, A0);
  not not_90 (not_90_out, G2);
  not not_91 (not_91_out, G3);
  not not_92 (not_92_out, A2);
  not not_93 (not_93_out, G2);
  not not_94 (not_94_out, G3);
  not not_95 (not_95_out, A1);
  not not_96 (not_96_out, G2);
  not not_97 (not_97_out, G3);
  not not_98 (not_98_out, A0);
  not not_99 (not_99_out, G2);
  not not_100 (not_100_out, G3);
  not not_101 (not_101_out, G2);
  not not_102 (not_102_out, G3);
  not not_103 (not_103_out, A2);
  not not_104 (not_104_out, A1);
  not not_105 (not_105_out, A0);
  not not_106 (not_106_out, G2);
  not not_107 (not_107_out, G3);
  not not_108 (not_108_out, A2);
  not not_109 (not_109_out, A1);
  not not_110 (not_110_out, G2);
  not not_111 (not_111_out, G3);
  not not_112 (not_112_out, A2);
  not not_113 (not_113_out, A0);
  not not_114 (not_114_out, G2);
  not not_115 (not_115_out, G3);
  not not_116 (not_116_out, A1);
  not not_117 (not_117_out, A0);
  not not_118 (not_118_out, G2);
  not not_119 (not_119_out, G3);
  not not_120 (not_120_out, A1);
  not not_121 (not_121_out, G2);
  not not_122 (not_122_out, G3);
  not not_123 (not_123_out, A0);
  not not_124 (not_124_out, G2);
  not not_125 (not_125_out, G3);
  not not_126 (not_126_out, G2);
  not not_127 (not_127_out, G3);
  not not_128 (not_128_out, A2);
  not not_129 (not_129_out, A1);
  not not_130 (not_130_out, A0);
  not not_131 (not_131_out, G2);
  not not_132 (not_132_out, G3);
  not not_133 (not_133_out, A2);
  not not_134 (not_134_out, A1);
  not not_135 (not_135_out, G2);
  not not_136 (not_136_out, G3);
  not not_137 (not_137_out, A2);
  not not_138 (not_138_out, G2);
  not not_139 (not_139_out, G3);
  not not_140 (not_140_out, A1);
  not not_141 (not_141_out, A0);
  not not_142 (not_142_out, G2);
  not not_143 (not_143_out, G3);
  not not_144 (not_144_out, A1);
  not not_145 (not_145_out, G2);
  not not_146 (not_146_out, G3);
  not not_147 (not_147_out, A0);
  not not_148 (not_148_out, G2);
  not not_149 (not_149_out, G3);
  not not_150 (not_150_out, G2);
  not not_151 (not_151_out, G3);
  not not_152 (not_152_out, A2);
  not not_153 (not_153_out, A1);
  not not_154 (not_154_out, A0);
  not not_155 (not_155_out, G2);
  not not_156 (not_156_out, G3);
  not not_157 (not_157_out, A2);
  not not_158 (not_158_out, A0);
  not not_159 (not_159_out, G2);
  not not_160 (not_160_out, G3);
  not not_161 (not_161_out, A2);
  not not_162 (not_162_out, G2);
  not not_163 (not_163_out, G3);
  not not_164 (not_164_out, A1);
  not not_165 (not_165_out, A0);
  not not_166 (not_166_out, G2);
  not not_167 (not_167_out, G3);
  not not_168 (not_168_out, A1);
  not not_169 (not_169_out, G2);
  not not_170 (not_170_out, G3);
  not not_171 (not_171_out, A0);
  not not_172 (not_172_out, G2);
  not not_173 (not_173_out, G3);
  not not_174 (not_174_out, G2);
  not not_175 (not_175_out, G3);
  not not_176 (not_176_out, A2);
  not not_177 (not_177_out, A1);
  not not_178 (not_178_out, G2);
  not not_179 (not_179_out, G3);
  not not_180 (not_180_out, A2);
  not not_181 (not_181_out, A0);
  not not_182 (not_182_out, G2);
  not not_183 (not_183_out, G3);
  not not_184 (not_184_out, A2);
  not not_185 (not_185_out, G2);
  not not_186 (not_186_out, G3);
  not not_187 (not_187_out, A1);
  not not_188 (not_188_out, A0);
  not not_189 (not_189_out, G2);
  not not_190 (not_190_out, G3);
  not not_191 (not_191_out, A1);
  not not_192 (not_192_out, G2);
  not not_193 (not_193_out, G3);
  not not_194 (not_194_out, A0);
  not not_195 (not_195_out, G2);
  not not_196 (not_196_out, G3);
  not not_197 (not_197_out, G1);
  and and_1 (and_1_out, G1, not_1_out, not_2_out, not_3_out, not_4_out, not_5_out);
  and and_2 (and_2_out, G1, not_6_out, not_7_out, not_8_out, not_9_out, A0);
  and and_3 (and_3_out, G1, not_10_out, not_11_out, not_12_out, A1, not_13_out);
  and and_4 (and_4_out, G1, not_14_out, not_15_out, not_16_out, A1, A0);
  and and_5 (and_5_out, G1, not_17_out, not_18_out, A2, not_19_out, not_20_out);
  and and_6 (and_6_out, G1, not_21_out, not_22_out, A2, not_23_out, A0);
  and and_7 (and_7_out, G1, not_24_out, not_25_out, A2, A1, not_26_out);
  not not_198 (not_198_out, G1);
  and and_8 (and_8_out, G1, not_27_out, not_28_out, not_29_out, not_30_out, not_31_out);
  and and_9 (and_9_out, G1, not_32_out, not_33_out, not_34_out, not_35_out, A0);
  and and_10 (and_10_out, G1, not_36_out, not_37_out, not_38_out, A1, not_39_out);
  and and_11 (and_11_out, G1, not_40_out, not_41_out, not_42_out, A1, A0);
  and and_12 (and_12_out, G1, not_43_out, not_44_out, A2, not_45_out, not_46_out);
  and and_13 (and_13_out, G1, not_47_out, not_48_out, A2, not_49_out, A0);
  and and_14 (and_14_out, G1, not_50_out, not_51_out, A2, A1, A0);
  not not_199 (not_199_out, G1);
  and and_15 (and_15_out, G1, not_52_out, not_53_out, not_54_out, not_55_out, not_56_out);
  and and_16 (and_16_out, G1, not_57_out, not_58_out, not_59_out, not_60_out, A0);
  and and_17 (and_17_out, G1, not_61_out, not_62_out, not_63_out, A1, not_64_out);
  and and_18 (and_18_out, G1, not_65_out, not_66_out, not_67_out, A1, A0);
  and and_19 (and_19_out, G1, not_68_out, not_69_out, A2, not_70_out, not_71_out);
  and and_20 (and_20_out, G1, not_72_out, not_73_out, A2, A1, not_74_out);
  and and_21 (and_21_out, G1, not_75_out, not_76_out, A2, A1, A0);
  not not_200 (not_200_out, G1);
  and and_22 (and_22_out, G1, not_77_out, not_78_out, not_79_out, not_80_out, not_81_out);
  and and_23 (and_23_out, G1, not_82_out, not_83_out, not_84_out, not_85_out, A0);
  and and_24 (and_24_out, G1, not_86_out, not_87_out, not_88_out, A1, not_89_out);
  and and_25 (and_25_out, G1, not_90_out, not_91_out, not_92_out, A1, A0);
  and and_26 (and_26_out, G1, not_93_out, not_94_out, A2, not_95_out, A0);
  and and_27 (and_27_out, G1, not_96_out, not_97_out, A2, A1, not_98_out);
  and and_28 (and_28_out, G1, not_99_out, not_100_out, A2, A1, A0);
  not not_201 (not_201_out, G1);
  and and_29 (and_29_out, G1, not_101_out, not_102_out, not_103_out, not_104_out, not_105_out);
  and and_30 (and_30_out, G1, not_106_out, not_107_out, not_108_out, not_109_out, A0);
  and and_31 (and_31_out, G1, not_110_out, not_111_out, not_112_out, A1, not_113_out);
  and and_32 (and_32_out, G1, not_114_out, not_115_out, A2, not_116_out, not_117_out);
  and and_33 (and_33_out, G1, not_118_out, not_119_out, A2, not_120_out, A0);
  and and_34 (and_34_out, G1, not_121_out, not_122_out, A2, A1, not_123_out);
  and and_35 (and_35_out, G1, not_124_out, not_125_out, A2, A1, A0);
  not not_202 (not_202_out, G1);
  and and_36 (and_36_out, G1, not_126_out, not_127_out, not_128_out, not_129_out, not_130_out);
  and and_37 (and_37_out, G1, not_131_out, not_132_out, not_133_out, not_134_out, A0);
  and and_38 (and_38_out, G1, not_135_out, not_136_out, not_137_out, A1, A0);
  and and_39 (and_39_out, G1, not_138_out, not_139_out, A2, not_140_out, not_141_out);
  and and_40 (and_40_out, G1, not_142_out, not_143_out, A2, not_144_out, A0);
  and and_41 (and_41_out, G1, not_145_out, not_146_out, A2, A1, not_147_out);
  and and_42 (and_42_out, G1, not_148_out, not_149_out, A2, A1, A0);
  not not_203 (not_203_out, G1);
  and and_43 (and_43_out, G1, not_150_out, not_151_out, not_152_out, not_153_out, not_154_out);
  and and_44 (and_44_out, G1, not_155_out, not_156_out, not_157_out, A1, not_158_out);
  and and_45 (and_45_out, G1, not_159_out, not_160_out, not_161_out, A1, A0);
  and and_46 (and_46_out, G1, not_162_out, not_163_out, A2, not_164_out, not_165_out);
  and and_47 (and_47_out, G1, not_166_out, not_167_out, A2, not_168_out, A0);
  and and_48 (and_48_out, G1, not_169_out, not_170_out, A2, A1, not_171_out);
  and and_49 (and_49_out, G1, not_172_out, not_173_out, A2, A1, A0);
  not not_204 (not_204_out, G1);
  and and_50 (and_50_out, G1, not_174_out, not_175_out, not_176_out, not_177_out, A0);
  and and_51 (and_51_out, G1, not_178_out, not_179_out, not_180_out, A1, not_181_out);
  and and_52 (and_52_out, G1, not_182_out, not_183_out, not_184_out, A1, A0);
  and and_53 (and_53_out, G1, not_185_out, not_186_out, A2, not_187_out, not_188_out);
  and and_54 (and_54_out, G1, not_189_out, not_190_out, A2, not_191_out, A0);
  and and_55 (and_55_out, G1, not_192_out, not_193_out, A2, A1, not_194_out);
  and and_56 (and_56_out, G1, not_195_out, not_196_out, A2, A1, A0);
  or or_1 (Y7, G2, G3, not_197_out, and_1_out, and_2_out, and_3_out, and_4_out, and_5_out, and_6_out, and_7_out);
  or or_2 (Y6, G2, G3, not_198_out, and_8_out, and_9_out, and_10_out, and_11_out, and_12_out, and_13_out, and_14_out);
  or or_3 (Y5, G2, G3, not_199_out, and_15_out, and_16_out, and_17_out, and_18_out, and_19_out, and_20_out, and_21_out);
  or or_4 (Y4, G2, G3, not_200_out, and_22_out, and_23_out, and_24_out, and_25_out, and_26_out, and_27_out, and_28_out);
  or or_5 (Y3, G2, G3, not_201_out, and_29_out, and_30_out, and_31_out, and_32_out, and_33_out, and_34_out, and_35_out);
  or or_6 (Y2, G2, G3, not_202_out, and_36_out, and_37_out, and_38_out, and_39_out, and_40_out, and_41_out, and_42_out);
  or or_7 (Y1, G2, G3, not_203_out, and_43_out, and_44_out, and_45_out, and_46_out, and_47_out, and_48_out, and_49_out);
  or or_8 (Y0, G2, G3, not_204_out, and_50_out, and_51_out, and_52_out, and_53_out, and_54_out, and_55_out, and_56_out);
endmodule

module exercise2_2 (
  input  G1,
  input  G2,
  input  G3,
  input  A2,
  input  A1,
  input  A0,
  output Y7,
  output Y6,
  output Y5,
  output Y4,
  output Y3,
  output Y2,
  output Y1,
  output Y0
);

  wire not_1_out, not_2_out, not_3_out, not_4_out, not_5_out, not_6_out, not_7_out, not_8_out, not_9_out,
       not_10_out, not_11_out, not_12_out, not_13_out, not_14_out, not_15_out, not_16_out, not_17_out,
       not_18_out, not_19_out, not_20_out;

  not not_1 (not_1_out, G1);
  not not_2 (not_2_out, A2);
  not not_3 (not_3_out, A1);
  not not_4 (not_4_out, A0);
  not not_5 (not_5_out, G1);
  not not_6 (not_6_out, A2);
  not not_7 (not_7_out, A1);
  not not_8 (not_8_out, G1);
  not not_9 (not_9_out, A2);
  not not_10 (not_10_out, A0);
  not not_11 (not_11_out, G1);
  not not_12 (not_12_out, A2);
  not not_13 (not_13_out, G1);
  not not_14 (not_14_out, A1);
  not not_15 (not_15_out, A0);
  not not_16 (not_16_out, G1);
  not not_17 (not_17_out, A1);
  not not_18 (not_18_out, G1);
  not not_19 (not_19_out, A0);
  not not_20 (not_20_out, G1);
  or or_1 (Y7, not_1_out, not_2_out, not_3_out, not_4_out, G3, G2);
  or or_2 (Y6, not_5_out, not_6_out, not_7_out, A0, G3, G2);
  or or_3 (Y5, not_8_out, not_9_out, not_10_out, A1, G3, G2);
  or or_4 (Y4, not_11_out, not_12_out, A0, A1, G3, G2);
  or or_5 (Y3, not_13_out, not_14_out, not_15_out, A2, G3, G2);
  or or_6 (Y2, not_16_out, not_17_out, A0, A2, G3, G2);
  or or_7 (Y1, not_18_out, not_19_out, A1, A2, G3, G2);
  or or_8 (Y0, not_20_out, A0, A1, A2, G3, G2);

  // Notes on the sheet:
  //   伍少枫 PE20110007
endmodule

module verilog_1 (
  input  in,
  output out,
  output out_n
);

  not not_1 (out_n, in);

  assign out = in;

  // Notes on the sheet:
  //   伍少枫 PE20110007
endmodule

module verilog_2 (
  input  a,
  input  b,
  output sum,
  output cout
);

  xor xor_1 (sum, a, b);
  and and_1 (cout, a, b);

  // Notes on the sheet:
  //   伍少枫 PE20110007
endmodule

module verilog_3 (
  input  a,
  input  b,
  input  cin,
  output sum,
  output cout
);

  wire verilog_2_1_cout, verilog_2_1_sum, verilog_2_2_cout;

  verilog_2 verilog_2_1 (.a(a), .b(b), .sum(verilog_2_1_sum), .cout(verilog_2_1_cout));
  verilog_2 verilog_2_2 (.a(verilog_2_1_sum), .b(cin), .sum(sum), .cout(verilog_2_2_cout));
  or or_1 (cout, verilog_2_2_cout, verilog_2_1_cout);

  // Notes on the sheet:
  //   s
  //   伍少枫 PE20110007
  //   carry1
  //   carry2
endmodule

module exercise3 (
  input  a,
  input  b,
  input  sel,
  output out
);


  // Notes on the sheet:
  //   伍少枫 PE20110007
endmodule

module exercise3_1 (
  input  a,
  input  b,
  input  sel,
  output out
);

  wire and_1_out, and_2_out, not_1_out;

  not not_1 (not_1_out, sel);
  and and_1 (and_1_out, b, sel);
  and and_2 (and_2_out, a, not_1_out);
  or or_1 (out, and_1_out, and_2_out);

  // Notes on the sheet:
  //   伍少枫 PE20110007
endmodule

module exercise4 (
  input  a,
  input  b,
  input  sel1,
  input  c,
  input  d,
  input  sel2,
  output out
);

  wire exercise3_1_1_out, exercise3_1_2_out, xor_1_out;

  exercise3_1 exercise3_1_1 (.a(a), .b(b), .sel(sel1), .out(exercise3_1_1_out));
  exercise3_1 exercise3_1_2 (.a(c), .b(d), .sel(sel2), .out(exercise3_1_2_out));
  xor xor_1 (xor_1_out, sel2, sel1);
  exercise3_1 exercise3_1_3 (.a(exercise3_1_1_out), .b(exercise3_1_2_out), .sel(xor_1_out), .out(out));

  // Notes on the sheet:
  //   inst1
  //   s1
  //   inst2
  //   s2
  //   伍少枫 PE20110007
  //   inst3
  //   s3
endmodule

module exercise_5 (
  input  i7,
  input  i6,
  input  i5,
  input  i4,
  input  i3,
  input  i2,
  input  i1,
  output y2,
  output y1,
  output y0
);
endmodule

module exercise6 (
  input  a,
  input  b,
  input  c,
  output s1,
  output s2
);
endmodule

module exercise6_1 (
  input  a,
  input  b,
  input  c,
  output s1,
  output s2
);

  wire and_1_out, and_2_out, and_3_out, and_4_out, and_5_out, and_6_out, and_7_out, and_8_out, not_1_out,
       not_2_out, not_3_out, not_4_out, not_5_out, not_6_out, not_7_out, not_8_out, not_9_out, not_10_out,
       not_11_out, not_12_out;

  not not_1 (not_1_out, a);
  not not_2 (not_2_out, b);
  not not_3 (not_3_out, a);
  not not_4 (not_4_out, c);
  not not_5 (not_5_out, b);
  not not_6 (not_6_out, c);
  not not_7 (not_7_out, a);
  not not_8 (not_8_out, b);
  not not_9 (not_9_out, c);
  not not_10 (not_10_out, a);
  not not_11 (not_11_out, b);
  not not_12 (not_12_out, c);
  and and_1 (and_1_out, not_1_out, not_2_out, c);
  and and_2 (and_2_out, not_3_out, b, not_4_out);
  and and_3 (and_3_out, a, not_5_out, not_6_out);
  and and_4 (and_4_out, a, b, c);
  and and_5 (and_5_out, not_7_out, b, c);
  and and_6 (and_6_out, a, not_8_out, c);
  and and_7 (and_7_out, a, b, not_9_out);
  and and_8 (and_8_out, not_10_out, not_11_out, not_12_out);
  or or_1 (s1, and_1_out, and_2_out, and_3_out, and_4_out);
  or or_2 (s2, and_5_out, and_6_out, and_7_out, and_8_out);

  // Notes on the sheet:
  //   伍少枫 PE20110007
endmodule
