// Logisim project exp3.circ as structural Verilog: 19 circuits, main circuit step1
module step1 (
  input  in_1,
  input  in_2,
  output Q,
  output nQ,
  output Q_2,
  output nQ_2
);

  not G1 (Q, nQ);
  not G2 (nQ, Q);
  not G1_2 (Q_2, nQ_2);
  not G2_2 (nQ_2, Q_2);

  // Notes on the sheet:
  //   伍少枫 PE20110007
  //   电路0状态
  //   电路1状态
endmodule

module step2 (
  input  R,
  input  \R_复位端 ,
  input  S,
  input  S_2,
  input  R_2,
  input  R_3,
  input  S_3,
  input  \S_置1端 ,
  output Q,
  output Q_2,
  output nQ,
  output nQ_2,
  output Q_3,
  output Q_4,
  output nQ_3,
  output nQ_4
);

  nor G1 (Q, R, nQ);
  nor G2 (nQ, Q, S);
  nor G1_2 (Q_3, R_2, nQ_3);
  nor G2_2 (nQ_3, Q_3, S_3);
  nor G1_3 (Q_2, \R_复位端 , nQ_2);
  nor G2_3 (nQ_2, Q_2, S_2);
  nor G1_4 (Q_4, R_3, nQ_4);
  nor G2_4 (nQ_4, Q_4, \S_置1端 );

  // Notes on the sheet:
  //   保持状态
  //   非定义状态
  //   SR锁存器
  //   伍少枫PE20110007
  //   置0
  //   置1
endmodule

module step2_1 (
  input  R,
  input  S,
  output Q,
  output nQ
);

  nor G1 (Q, R, nQ);
  nor G2 (nQ, Q, S);

  // Notes on the sheet:
  //   保持状态
endmodule

module step3 (
  input  CLK,
  input  CLK_2,
  input  D,
  input  D_2,
  input  CLK_3,
  input  CLK_4,
  input  D_3,
  input  D_4,
  input  CLK_5,
  input  D_5,
  output Q,
  output Q_2,
  output nQ,
  output nQ_2,
  output Q_3,
  output Q_4,
  output nQ_3,
  output nQ_4,
  output Q_5,
  output nQ_5
);

  wire G3_2_out, G3_3_out, G3_4_out, G3_out, G4_2_out, G4_3_out, G4_4_out, G4_out, nand_1_out, nand_2_out,
       not_1_out, not_2_out, not_3_out, not_4_out, not_5_out;

  not not_1 (not_1_out, D);
  not not_2 (not_2_out, D_3);
  and G4 (G4_out, CLK, not_1_out);
  and G3 (G3_out, CLK, D);
  and G4_2 (G4_2_out, CLK_3, not_2_out);
  and G3_2 (G3_2_out, CLK_3, D_3);
  nor G1 (Q, G4_out, nQ);
  nor G2 (nQ, Q, G3_out);
  nor G1_2 (Q_3, G4_2_out, nQ_3);
  nor G2_2 (nQ_3, Q_3, G3_2_out);
  not not_3 (not_3_out, D_5);
  nand nand_1 (nand_1_out, CLK_5, not_3_out);
  nand nand_2 (nand_2_out, CLK_5, D_5);
  not not_4 (not_4_out, D_2);
  not not_5 (not_5_out, D_4);
  nand nand_3 (Q_5, nand_1_out, nQ_5);
  nand nand_4 (nQ_5, Q_5, nand_2_out);
  and G4_3 (G4_3_out, CLK_2, not_4_out);
  and G3_3 (G3_3_out, CLK_2, D_2);
  and G4_4 (G4_4_out, CLK_4, not_5_out);
  and G3_4 (G3_4_out, CLK_4, D_4);
  nor G1_3 (Q_2, G4_3_out, nQ_2);
  nor G2_3 (nQ_2, Q_2, G3_3_out);
  nor G1_4 (Q_4, G4_4_out, nQ_4);
  nor G2_4 (nQ_4, Q_4, G3_4_out);

  // Notes on the sheet:
  //   保持
  //   R
  //   S
  //   置0
  //   R
  //   S
  //   伍少枫 PE20110007
  //   R
  //   S
  //   保持
  //   R
  //   S
  //   置1
  //   R
  //   S
endmodule

module step3_1 (
  input  CLK,
  input  D,
  output Q,
  output nQ
);

  wire G3_out, G4_out, not_1_out;

  not not_1 (not_1_out, D);
  and G4 (G4_out, CLK, not_1_out);
  and G3 (G3_out, CLK, D);
  nor G1 (Q, G4_out, nQ);
  nor G2 (nQ, Q, G3_out);

  // Notes on the sheet:
  //   R
  //   S
endmodule

module step4 (
  input  CLK,
  input  D,
  output Q,
  output nQ
);

  wire D1_q, not_1_out;

  not not_1 (not_1_out, CLK);
  step3_1 D1 (.CLK(not_1_out), .D(D), .Q(D1_q));  // open: nQ
  step3_1 D2 (.CLK(CLK), .D(D1_q), .Q(Q), .nQ(nQ));

  // Notes on the sheet:
  //   伍少枫 PE20110007
endmodule

module step4_1 (
  input  CLK,
  input  D,
  input  nRST,
  output Q,
  output nQ
);

  wire and_1_out, D1_q, not_1_out;

  not not_1 (not_1_out, CLK);
  and and_1 (and_1_out, D, nRST);
  step3_1 D1 (.CLK(not_1_out), .D(and_1_out), .Q(D1_q));  // open: nQ
  step3_1 D2 (.CLK(CLK), .D(D1_q), .Q(Q), .nQ(nQ));

  // Notes on the sheet:
  //   伍少枫 PE20110007
endmodule

module step4_2 (
  input  D,
  input  nRST,
  input  nRST_2,
  input  D_2,
  output Q,
  output nQ,
  output out_7,
  output out_8
);

  wire and_1_out, and_2_out, and_3_out, and_4_out, and_5_out, CLK_2_out, CLK_out, not_1_out, not_2_out,
       not_3_out, not_4_out, or_1_out, step4_3_1_out, step4_3_2_out;

  Clock CLK (.out(CLK_out));
  not not_1 (not_1_out, D);
  Clock CLK_2 (.out(CLK_2_out));
  not not_2 (not_2_out, not_1_out);
  and and_1 (and_1_out, not_2_out, nRST);
  and and_2 (and_2_out, CLK_2_out, not_3_out);
  not not_3 (not_3_out, D_2);
  and and_3 (and_3_out, CLK_2_out, D_2);
  and and_4 (and_4_out, CLK_out, and_1_out);
  or or_1 (or_1_out, and_4_out, not_4_out);
  not not_4 (not_4_out, nRST);
  step4_3 step4_3_1 (.A(1'b1), .B(and_2_out), .S(nRST_2), .out(step4_3_1_out));
  step4_3 step4_3_2 (.A(1'b0), .B(and_3_out), .S(nRST_2), .out(step4_3_2_out));
  and and_5 (and_5_out, CLK_out, not_1_out, nRST);
  step2_1 step2_1_1 (.R(step4_3_1_out), .S(step4_3_2_out), .Q(out_7), .nQ(out_8));
  step2_1 step2_1_2 (.R(and_5_out), .S(or_1_out), .Q(Q), .nQ(nQ));

  // Notes on the sheet:
  //   伍少枫 PE20110007
endmodule

module step4_3 (
  input  A,
  input  B,
  input  S,
  output out
);

  wire and_1_out, and_2_out, not_1_out;

  and and_1 (and_1_out, A, not_1_out);
  not not_1 (not_1_out, S);
  and and_2 (and_2_out, B, S);
  or or_1 (out, and_1_out, and_2_out);
endmodule

module test (
  input  RST,
  input  CLK,
  input  D,
  input  in_4,
  input  in_5,
  input  in_6,
  input  CLK_2,
  input  RST_2,
  input  D_2,
  output out_10,
  output out_11,
  output out_12,
  output out_13,
  output nQ,
  output out_15,
  output nQ_2,
  output out_17
);

  wire and_1_out, nand_1_out, not_1_out, step3_1_1_q, step3_2_1_q, step3_2_2_q, step3_2_3_q, undriven,
       undriven_2, undriven_3;

  nand nand_1 (nand_1_out, CLK_2, RST_2);
  step3_2 step3_2_1 (.CLK(CLK), .D(RST), .Q(step3_2_1_q));  // open: nQ
  D_Flip_Flop d_ff_1 (.clk(in_4), .D(in_5), .Q(out_13), .reset(in_6));  // open: Qn, preset, en
  not not_1 (not_1_out, nand_1_out);
  step3_1 step3_1_1 (.D(D_2), .Q(step3_1_1_q));  // open: CLK, nQ
  step3_2 step3_2_2 (.CLK(CLK), .D(D), .Q(step3_2_2_q), .nQ(out_12));
  buf and_1 (and_1_out, step3_2_1_q);  // AND_Gate
  step3_1 step3_1_2 (.CLK(not_1_out), .D(step3_1_1_q), .Q(out_17));  // open: nQ
  step3_2 step3_2_3 (.CLK(CLK), .Q(step3_2_3_q));  // open: D, nQ
  D_Flip_Flop d_ff_2 ();  // open: clk, D, Q, Qn, preset, en, reset
  and and_2 (out_10, step3_2_3_q, RST);
  buf and_3 (out_11, step3_2_2_q);  // AND_Gate
  step4_3 step4_3_1 (.A(undriven), .B(undriven_2), .S(undriven_3), .out(out_15));
endmodule

module step3_2 (
  input  CLK,
  input  D,
  output Q,
  output nQ
);

  wire G1_out, G2_out, G3_2_out, G3_out, G4_2_out, G4_out, not_1_out, not_2_out, not_3_out;

  not not_1 (not_1_out, CLK);
  not not_2 (not_2_out, D);
  and G4 (G4_out, not_1_out, not_2_out);
  and G3 (G3_out, not_1_out, D);
  nor G1 (G1_out, G4_out, G2_out);
  nor G2 (G2_out, G1_out, G3_out);
  not not_3 (not_3_out, G1_out);
  and G4_2 (G4_2_out, CLK, not_3_out);
  and G3_2 (G3_2_out, CLK, G1_out);
  nor G1_2 (Q, G4_2_out, nQ);
  nor G2_2 (nQ, Q, G3_2_out);

  // Notes on the sheet:
  //   R
  //   S
  //   R
  //   S
endmodule

module e3_1 (
  input  D,
  input  RST,
  input  CLK,
  output out_4,
  output Q
);

  wire nand_1_out, nand_2_out, nand_3_out, nand_4_out, nand_5_out, nand_6_out, not_1_out, not_2_out;

  nand nand_1 (nand_1_out, nand_5_out, D);
  not not_1 (not_1_out, CLK);
  nand nand_2 (nand_2_out, RST, not_1_out);
  nand nand_3 (nand_3_out, nand_1_out, nand_6_out);
  nand nand_4 (nand_4_out, RST, nand_3_out);
  not not_2 (not_2_out, nand_4_out);
  nand nand_5 (nand_5_out, nand_4_out, nand_2_out);
  nand nand_6 (nand_6_out, nand_2_out, not_2_out);
  nand nand_7 (out_4, nand_5_out, Q);
  nand nand_8 (Q, out_4, nand_6_out);

  // Notes on the sheet:
  //   伍少枫 PE20110007
endmodule

module step5_1 (
  input  [3:0] D_IN,
  input  CLK,
  input  RST_N,
  input  [3:0] D_IN_2,
  input  CLK_2,
  input  RST_N_2,
  output [3:0] D_OUT,
  output [3:0] D_OUT_2
);

  wire and_1_out, and_2_out, and_3_out, and_4_out, and_5_out, and_6_out, and_7_out, and_8_out, not_1_out,
       or_1_out, or_2_out;

  not not_1 (not_1_out, RST_N_2);
  and and_1 (and_1_out, D_IN[0], RST_N);
  and and_2 (and_2_out, D_IN[1], RST_N);
  and and_3 (and_3_out, D_IN[2], RST_N);
  and and_4 (and_4_out, D_IN[3], RST_N);
  and and_5 (and_5_out, D_IN_2[3], RST_N_2);
  and and_6 (and_6_out, D_IN_2[2], RST_N_2);
  and and_7 (and_7_out, D_IN_2[1], RST_N_2);
  and and_8 (and_8_out, D_IN_2[0], RST_N_2);
  or or_1 (or_1_out, and_7_out, not_1_out);
  or or_2 (or_2_out, and_8_out, not_1_out);
  step3_2 step3_2_1 (.CLK(CLK_2), .D(and_5_out), .Q(D_OUT_2[3]));  // open: nQ
  step3_2 step3_2_2 (.CLK(CLK_2), .D(and_6_out), .Q(D_OUT_2[2]));  // open: nQ
  step3_2 step3_2_3 (.CLK(CLK_2), .D(or_1_out), .Q(D_OUT_2[1]));  // open: nQ
  step3_2 step3_2_4 (.CLK(CLK_2), .D(or_2_out), .Q(D_OUT_2[0]));  // open: nQ

  // Notes on the sheet:
  //   伍少枫 PE20110007
  //   伍少枫 PE20110007
endmodule

module step6_1 (
  input  in_1,
  input  in_2,
  output out_3,
  output [3:0] CNT
);

  wire [3:0] adder_1_out;

  Adder #(.width(4)) adder_1 (.a(CNT), .b(4'b0001), .out(adder_1_out), .cin(1'b0), .cout(out_3));
  step5_1 step5_1_1 (
    .D_IN(adder_1_out), .CLK(in_1), .RST_N(in_2), .D_OUT(CNT));  // open: D_IN_2, D_OUT_2, CLK_2, RST_N_2

  // Notes on the sheet:
  //   伍少枫 PE20110007
endmodule

module e1 (
  input  R,
  input  S,
  output Q,
  output nQ
);

  nand nand_1 (Q, R, nQ);
  nand nand_2 (nQ, Q, S);

  // Notes on the sheet:
  //   伍少枫 PE20110007
endmodule

module e3 (
  input  RST,
  input  CLK,
  output [3:0] CNT,
  output out_4
);

  wire [3:0] adder_1_out;

  Adder #(.width(4)) adder_1 (.a(CNT), .b(4'b0001), .out(adder_1_out), .cin(1'b0), .cout(out_4));
  e3_1 e3_1_1 (.D(adder_1_out[0]), .RST(RST), .Q(CNT[0]), .CLK(CLK));  // open: out_4
  e3_1 e3_1_2 (.D(adder_1_out[1]), .RST(RST), .Q(CNT[1]), .CLK(CLK));  // open: out_4
  e3_1 e3_1_3 (.D(adder_1_out[2]), .RST(RST), .Q(CNT[2]), .CLK(CLK));  // open: out_4
  e3_1 e3_1_4 (.D(adder_1_out[3]), .RST(RST), .Q(CNT[3]), .CLK(CLK));  // open: out_4

  // Notes on the sheet:
  //   伍少枫 PE20110007
endmodule

module e4 (
  input  CLK,
  input  RST,
  output [3:0] CNT,
  output out_4
);

  wire and_1_out, nand_1_out;
  wire [3:0] adder_1_out, step4_1_1_q;

  Adder #(.width(4)) adder_1 (.a(step4_1_1_q), .b(4'b0001), .out(adder_1_out), .cin(1'b0), .cout(out_4));
  Subtractor #(.width(4)) subtractor_1 (.a(4'b1001), .b(step4_1_1_q), .out(CNT));  // open: bin, bout
  and and_1 (and_1_out, RST, nand_1_out);
  step4_1 step4_1_1 (.CLK(CLK), .D(adder_1_out[0]), .nRST(and_1_out), .Q(step4_1_1_q[0]));  // open: nQ
  step4_1 step4_1_2 (.CLK(CLK), .D(adder_1_out[1]), .nRST(and_1_out), .Q(step4_1_1_q[1]));  // open: nQ
  step4_1 step4_1_3 (.CLK(CLK), .D(adder_1_out[2]), .nRST(and_1_out), .Q(step4_1_1_q[2]));  // open: nQ
  step4_1 step4_1_4 (.CLK(CLK), .D(adder_1_out[3]), .nRST(and_1_out), .Q(step4_1_1_q[3]));  // open: nQ
  nand nand_1 (nand_1_out, step4_1_1_q[3], step4_1_1_q[0]);

  // Notes on the sheet:
  //   伍少枫 PE20110007
endmodule

module e2 (
  input  D,
  input  SET,
  output Q
);

  wire CLK_out, not_1_out, or_1_out, step3_1_1_q;

  Clock CLK (.out(CLK_out));
  not not_1 (not_1_out, CLK_out);
  or or_1 (or_1_out, D, SET);
  step3_1 step3_1_1 (.CLK(not_1_out), .D(or_1_out), .Q(step3_1_1_q));  // open: nQ
  step3_1 step3_1_2 (.CLK(CLK_out), .D(step3_1_1_q), .Q(Q));  // open: nQ

  // Notes on the sheet:
  //   伍少枫 PE20110007
endmodule

module e5 (
  input  CLK,
  input  D,
  input  nRST,
  output Q,
  output nQ
);

  wire and_1_out, D1_q, not_1_out, not_2_out;

  not not_1 (not_1_out, nRST);
  not not_2 (not_2_out, CLK);
  and and_1 (and_1_out, D, not_1_out);
  step3_1 D1 (.CLK(not_2_out), .D(and_1_out), .Q(D1_q));  // open: nQ
  step3_1 D2 (.CLK(CLK), .D(D1_q), .Q(Q), .nQ(nQ));

  // Notes on the sheet:
  //   伍少枫 PE20110007
endmodule
