// Logisim project exp6.circ as structural Verilog: 5 circuits, main circuit 3_1
module _3_1 (
  input  [1:0] in_1,
  output out_2
);

  RAM #(.addrWidth(2), .dataWidth(1)) ram_1 (.addr(in_1), .data(out_2));  // open: sel, clk, ld, clr

  // Notes on the sheet:
  //   PE20110007 伍少枫
endmodule

module _3_2 (
  input  CLK,
  input  [1:0] in_2,
  input  in_3,
  output out_4
);

  wire d_ff_1_q, ram_1_data;

  RAM #(.addrWidth(2), .dataWidth(1)) ram_1 (.addr(in_2), .data(ram_1_data));  // open: sel, clk, ld, clr
  D_Flip_Flop d_ff_1 (.clk(CLK), .D(ram_1_data), .Q(d_ff_1_q));  // open: Qn, preset, en, reset
  Multiplexer multiplexer_1 (.in0(d_ff_1_q), .in1(ram_1_data), .out(out_4), .sel(in_3));  // open: en

  // Notes on the sheet:
  //   PE20110007 伍少枫
endmodule

module _4_1 (
  input  Input_1,
  input  Input_2,
  input  Input_3,
  input  [1:0] in_4,
  input  [1:0] in_5,
  input  [1:0] in_6,
  output Output_1,
  output Output_2,
  output Output_3
);

  wire decoder_1_out1, decoder_1_out2, decoder_1_out3, decoder_2_out1, decoder_2_out2, decoder_2_out3,
       decoder_3_out1, decoder_3_out2, decoder_3_out3;

  assign Output_1 = decoder_1_out1 ? Input_1 : 1'bz;  // Controlled_Buffer controlled_buffer_1
  assign Output_1 = decoder_1_out2 ? Input_2 : 1'bz;  // Controlled_Buffer controlled_buffer_2
  assign Output_1 = decoder_1_out3 ? Input_3 : 1'bz;  // Controlled_Buffer controlled_buffer_3
  Decoder #(.select(2)) decoder_1 (
    .out1(decoder_1_out1), .out2(decoder_1_out2), .out3(decoder_1_out3), .sel(in_4));  // open: out0, en
  Decoder #(.select(2)) decoder_2 (
    .out1(decoder_2_out1), .out2(decoder_2_out2), .out3(decoder_2_out3), .sel(in_5));  // open: out0, en
  assign Output_2 = decoder_2_out1 ? Input_1 : 1'bz;  // Controlled_Buffer controlled_buffer_4
  assign Output_2 = decoder_2_out2 ? Input_2 : 1'bz;  // Controlled_Buffer controlled_buffer_5
  assign Output_2 = decoder_2_out3 ? Input_3 : 1'bz;  // Controlled_Buffer controlled_buffer_6
  Decoder #(.select(2)) decoder_3 (
    .out1(decoder_3_out1), .out2(decoder_3_out2), .out3(decoder_3_out3), .sel(in_6));  // open: out0, en
  assign Output_3 = decoder_3_out1 ? Input_1 : 1'bz;  // Controlled_Buffer controlled_buffer_7
  assign Output_3 = decoder_3_out2 ? Input_2 : 1'bz;  // Controlled_Buffer controlled_buffer_8
  assign Output_3 = decoder_3_out3 ? Input_3 : 1'bz;  // Controlled_Buffer controlled_buffer_9

  // Notes on the sheet:
  //   PE20110007 伍少枫
endmodule

module _4_2 (
  input  Input_1,
  input  CLK,
  input  Input_2,
  input  a,
  input  b,
  input  in_6,
  input  in_7,
  input  [1:0] in_8,
  input  [1:0] in_9,
  input  [1:0] in_10,
  output Output_1,
  output Output_2,
  output Output_3,
  output out_14
);

  wire controlled_buffer_10_out, d_ff_1_q, decoder_1_out1, decoder_1_out2, decoder_1_out3, decoder_2_out1,
       decoder_2_out2, decoder_2_out3, decoder_3_out1, decoder_3_out2, decoder_3_out3, multiplexer_2_out,
       ram_1_data, undriven;
  wire [0:0] multiplexer_1_out;

  Multiplexer multiplexer_1 (.in0(Output_1), .in1(a), .out(multiplexer_1_out[0]), .sel(in_6));  // open: en
  RAM #(.addrWidth(2), .dataWidth(1)) ram_1 (
    .addr({b, multiplexer_1_out[0]}), .data(ram_1_data));  // open: sel, clk, ld, clr
  D_Flip_Flop d_ff_1 (.clk(CLK), .D(ram_1_data), .Q(d_ff_1_q));  // open: Qn, preset, en, reset
  Multiplexer multiplexer_2 (.in0(d_ff_1_q), .in1(ram_1_data), .out(multiplexer_2_out), .sel(in_7));  // open: en
  assign Output_1 = decoder_1_out1 ? Input_1 : 1'bz;  // Controlled_Buffer controlled_buffer_1
  assign Output_1 = decoder_1_out2 ? Input_2 : 1'bz;  // Controlled_Buffer controlled_buffer_2
  assign Output_1 = decoder_1_out3 ? multiplexer_2_out : 1'bz;  // Controlled_Buffer controlled_buffer_3
  Decoder #(.select(2)) decoder_1 (
    .out1(decoder_1_out1), .out2(decoder_1_out2), .out3(decoder_1_out3), .sel(in_8));  // open: out0, en
  Decoder #(.select(2)) decoder_2 (
    .out1(decoder_2_out1), .out2(decoder_2_out2), .out3(decoder_2_out3), .sel(in_9));  // open: out0, en
  assign Output_2 = decoder_2_out1 ? Input_1 : 1'bz;  // Controlled_Buffer controlled_buffer_4
  assign Output_2 = decoder_2_out2 ? Input_2 : 1'bz;  // Controlled_Buffer controlled_buffer_5
  assign Output_2 = decoder_2_out3 ? multiplexer_2_out : 1'bz;  // Controlled_Buffer controlled_buffer_6
  Decoder #(.select(2)) decoder_3 (
    .out1(decoder_3_out1), .out2(decoder_3_out2), .out3(decoder_3_out3), .sel(in_10));  // open: out0, en
  assign Output_3 = decoder_3_out1 ? Input_1 : 1'bz;  // Controlled_Buffer controlled_buffer_7
  assign Output_3 = decoder_3_out2 ? Input_2 : 1'bz;  // Controlled_Buffer controlled_buffer_8
  assign Output_3 = decoder_3_out3 ? multiplexer_2_out : 1'bz;  // Controlled_Buffer controlled_buffer_9
  Controlled_Buffer controlled_buffer_10 (.in(out_14), .out(controlled_buffer_10_out));  // open: en
  assign out_14 = undriven ? Output_3 : 1'bz;  // Controlled_Buffer controlled_buffer_11

  // Notes on the sheet:
  //   PE20110007 伍少枫
endmodule

module e1 (
  input  Input_1,
  input  CLK,
  input  Input_2,
  input  in_4,
  input  in_5,
  input  in_6,
  input  in_7,
  input  [1:0] in_8,
  input  [1:0] in_9,
  input  [1:0] in_10,
  input  in_11,
  output a,
  output Output_2,
  output Output_3,
  output B
);

  wire controlled_buffer_10_out, d_ff_1_q, decoder_1_out1, decoder_1_out2, decoder_1_out3, decoder_2_out1,
       decoder_2_out2, decoder_2_out3, decoder_3_out1, decoder_3_out2, decoder_3_out3, multiplexer_2_out,
       ram_1_data;
  wire [0:0] multiplexer_1_out;

  Multiplexer multiplexer_1 (.in0(a), .in1(in_4), .out(multiplexer_1_out[0]), .sel(in_6));  // open: en
  RAM #(.addrWidth(2), .dataWidth(1)) ram_1 (
    .addr({in_5, multiplexer_1_out[0]}), .data(ram_1_data));  // open: sel, clk, ld, clr
  D_Flip_Flop d_ff_1 (.clk(CLK), .D(ram_1_data), .Q(d_ff_1_q));  // open: Qn, preset, en, reset
  Multiplexer multiplexer_2 (.in0(d_ff_1_q), .in1(ram_1_data), .out(multiplexer_2_out), .sel(in_7));  // open: en
  assign a = decoder_1_out1 ? Input_1 : 1'bz;  // Controlled_Buffer controlled_buffer_1
  assign a = decoder_1_out2 ? Input_2 : 1'bz;  // Controlled_Buffer controlled_buffer_2
  assign a = decoder_1_out3 ? multiplexer_2_out : 1'bz;  // Controlled_Buffer controlled_buffer_3
  Decoder #(.select(2)) decoder_1 (
    .out1(decoder_1_out1), .out2(decoder_1_out2), .out3(decoder_1_out3), .sel(in_8));  // open: out0, en
  Decoder #(.select(2)) decoder_2 (
    .out1(decoder_2_out1), .out2(decoder_2_out2), .out3(decoder_2_out3), .sel(in_9));  // open: out0, en
  assign Output_2 = decoder_2_out1 ? Input_1 : 1'bz;  // Controlled_Buffer controlled_buffer_4
  assign Output_2 = decoder_2_out2 ? Input_2 : 1'bz;  // Controlled_Buffer controlled_buffer_5
  assign Output_2 = decoder_2_out3 ? multiplexer_2_out : 1'bz;  // Controlled_Buffer controlled_buffer_6
  Decoder #(.select(2)) decoder_3 (
    .out1(decoder_3_out1), .out2(decoder_3_out2), .out3(decoder_3_out3), .sel(in_10));  // open: out0, en
  assign Output_3 = decoder_3_out1 ? Input_1 : 1'bz;  // Controlled_Buffer controlled_buffer_7
  assign Output_3 = decoder_3_out2 ? Input_2 : 1'bz;  // Controlled_Buffer controlled_buffer_8
  assign Output_3 = decoder_3_out3 ? multiplexer_2_out : 1'bz;  // Controlled_Buffer controlled_buffer_9
  Controlled_Buffer controlled_buffer_10 (.in(B), .out(controlled_buffer_10_out));  // open: en
  assign B = in_11 ? a : 1'bz;  // Controlled_Buffer controlled_buffer_11

  // Notes on the sheet:
  //   PE20110007 伍少枫
endmodule
