// Logisim project exp8.circ as structural Verilog: 4 circuits, main circuit step2
module step2 (
  input  in_1,
  input  in_2,
  output out_3
);

  wire d_ff_1_q, d_ff_2_q, not_1_out;

  D_Flip_Flop d_ff_1 (.clk(in_1), .D(in_2), .Q(d_ff_1_q));  // open: Qn, preset, en, reset
  D_Flip_Flop d_ff_2 (.clk(in_1), .D(d_ff_1_q), .Q(d_ff_2_q));  // open: Qn, preset, en, reset
  not not_1 (not_1_out, d_ff_2_q);
  and and_1 (out_3, not_1_out, d_ff_1_q);

  // Notes on the sheet:
  //   PE20110007 伍少枫
endmodule

module step3 (
  input  clk,
  input  rst,
  input  time_pulse,
  output [1:0] next_state,
  output [1:0] current_state
);

  wire comparator_1_eq, comparator_2_eq, comparator_3_eq;
  wire [1:0] multiplexer_1_out;

  Multiplexer #(.select(2), .width(2), .enable("false")) multiplexer_1 (
    .in0(2'b01), .in1(2'b10), .in2(2'b00), .in3(2'b00), .out(multiplexer_1_out), .sel(current_state));
  Multiplexer #(.width(2), .enable("false")) multiplexer_2 (
    .in0(current_state), .in1(multiplexer_1_out), .out(next_state), .sel(time_pulse));
  Register #(.width(2)) register_1 (.D(next_state), .Q(current_state), .clk(clk), .clr(rst));  // open: en
  Comparator #(.width(2)) comparator_1 (.a(current_state), .b(2'b00), .eq(comparator_1_eq));  // open: gt, lt
  LED led_1 (.in(comparator_1_eq));
  LED led_2 (.in(comparator_2_eq));
  Comparator #(.width(2)) comparator_2 (.a(current_state), .b(2'b01), .eq(comparator_2_eq));  // open: gt, lt
  Comparator #(.width(2)) comparator_3 (.a(current_state), .b(2'b10), .eq(comparator_3_eq));  // open: gt, lt
  LED led_3 (.in(comparator_3_eq));

  // Notes on the sheet:
  //   PE20110007 伍少枫
endmodule

module step5 (
  input  clk,
  input  rst
);

  wire comparator_1_eq;
  wire [1:0] adder_1_out, register_1_q;

  Adder #(.width(2)) adder_1 (.a(register_1_q), .b(2'b00), .out(adder_1_out), .cin(1'b1));  // open: cout
  Register #(.width(2)) register_1 (.D(adder_1_out), .Q(register_1_q), .clk(clk), .clr(rst));  // open: en
  LED led (.in(comparator_1_eq));
  Comparator #(.width(2)) comparator_1 (.a(register_1_q), .b(2'b11), .eq(comparator_1_eq));  // open: gt, lt

  // Notes on the sheet:
  //   cnt+1
  //   PE20110007 伍少枫
  //   cnt
endmodule

module e2 (
  input  clk,
  input  rst,
  input  sw,
  output [3:0] out_4
);

  wire and_1_out, not_1_out, not_2_out;
  wire [3:0] adder_1_out, register_1_q, register_2_q;

  Adder #(.width(4)) adder_1 (.a(out_4), .b(4'b0000), .out(adder_1_out), .cin(1'b1));  // open: cout
  not not_1 (not_1_out, sw);
  Register #(.width(4)) register_1 (.D(adder_1_out), .Q(register_1_q), .clk(sw), .clr(and_1_out));  // open: en
  Register #(.width(4)) register_2 (.D(adder_1_out), .Q(register_2_q), .clk(not_1_out), .clr(and_1_out));  // open: en
  and and_1 (and_1_out, clk, rst);
  not not_2 (not_2_out, sw);
  Multiplexer #(.width(4)) multiplexer_1 (
    .in0(register_1_q), .in1(register_2_q), .out(out_4), .sel(not_2_out));  // open: en

  // Notes on the sheet:
  //   PE20110007 伍少枫
endmodule
